// Logisim project lab_6_1.circ as structural Verilog: 1 circuit, main circuit main
module main (
  input  C0,
  input  A0,
  input  A1,
  input  A2,
  input  A3,
  input  B0,
  input  B1,
  input  B2,
  input  B3,
  output S0,
  output S1,
  output S2,
  output S3,
  output Ca4
);

  wire and_1_out, and_2_out, and_3_out, and_4_out, and_5_out, and_6_out, and_7_out, and_8_out, and_9_out,
       and_10_out, and_11_out, and_12_out, C1_out, C2_out, C3_out, G0_out, G1_out, G2_out, G3_out, or_1_out,
       or_2_out, or_3_out, or_4_out, or_5_out, or_6_out, P0_out, P0C0_out, P1_out, P1C1_out, P2_out,
       P2C2_out, P3_out, P3C3_out, xor_1_out, xor_2_out, xor_3_out, xor_4_out, xor_5_out, xor_6_out,
       xor_7_out, xor_9_out, xor_11_out, xor_13_out;

  xor P2 (P2_out, A2, B2);
  and G2 (G2_out, A2, B2);
  xor xor_1 (xor_1_out, A2, B2);
  and and_1 (and_1_out, A2, B2);
  xor P3 (P3_out, A3, B3);
  and G3 (G3_out, A3, B3);
  xor xor_2 (xor_2_out, A0, B0);
  xor P1 (P1_out, A1, B1);
  and G1 (G1_out, A1, B1);
  and and_2 (and_2_out, A1, B1);
  and and_3 (and_3_out, A1, B1);
  xor P0 (P0_out, A0, B0);
  and G0 (G0_out, A0, B0);
  and and_4 (and_4_out, A0, B0);
  xor xor_3 (xor_3_out, A0, B0);
  and and_5 (and_5_out, A0, B0);
  xor xor_4 (xor_4_out, A1, B1);
  xor xor_5 (xor_5_out, A0, B0);
  and and_6 (and_6_out, A0, B0);
  xor xor_6 (xor_6_out, A1, B1);
  and and_7 (and_7_out, C0, xor_2_out);
  and and_8 (and_8_out, C0, xor_3_out);
  and and_9 (and_9_out, C0, xor_5_out);
  and P0C0 (P0C0_out, C0, P0_out);
  or or_1 (or_1_out, and_7_out, and_4_out);
  or C1 (C1_out, P0C0_out, G0_out);
  or or_2 (or_2_out, and_8_out, and_5_out);
  or or_3 (or_3_out, and_9_out, and_6_out);
  and P1C1 (P1C1_out, or_1_out, P1_out);
  and and_10 (and_10_out, or_2_out, xor_4_out);
  and and_11 (and_11_out, or_3_out, xor_6_out);
  or C2 (C2_out, P1C1_out, G1_out);
  or or_4 (or_4_out, and_10_out, and_2_out);
  or or_5 (or_5_out, and_11_out, and_3_out);
  xor xor_7 (xor_7_out, C0, A0);
  xor xor_8 (S0, xor_7_out, B0);
  xor xor_9 (xor_9_out, C1_out, A1);
  xor xor_10 (S1, xor_9_out, B1);
  xor xor_11 (xor_11_out, C2_out, A2);
  and P2C2 (P2C2_out, or_4_out, P2_out);
  and and_12 (and_12_out, or_5_out, xor_1_out);
  xor xor_12 (S2, xor_11_out, B2);
  or C3 (C3_out, P2C2_out, G2_out);
  or or_6 (or_6_out, and_12_out, and_1_out);
  and P3C3 (P3C3_out, or_6_out, P3_out);
  xor xor_13 (xor_13_out, C3_out, A3);
  xor xor_14 (S3, xor_13_out, B3);
  or C4 (Ca4, P3C3_out, G3_out);
endmodule
