// Logisim project universe.circ as structural Verilog: 1 circuit, main circuit main
module main (
  input  in_1,
  input  in_2,
  input  in_3,
  input  in_4,
  input  in_5,
  input  in_6,
  input  [1:0] in_7,
  input  in_8,
  output out_9,
  output out_10,
  output out_11,
  output out_12
);

  wire clock_1_out, multiplexer_1_out, multiplexer_2_out, multiplexer_3_out, multiplexer_4_out;

  Clock clock_1 (.out(clock_1_out));
  D_Flip_Flop d_ff_1 (.D(multiplexer_1_out), .clk(clock_1_out), .Q(out_11), .reset(in_8));  // open: Qn, preset
  Multiplexer #(.select(2)) multiplexer_1 (
    .in0(out_11), .in1(in_6), .in2(out_12), .in3(in_1), .out(multiplexer_1_out), .sel(in_7));
  Multiplexer #(.select(2)) multiplexer_2 (
    .in0(out_12), .in1(out_11), .in2(out_9), .in3(in_2), .out(multiplexer_2_out), .sel(in_7));
  D_Flip_Flop d_ff_2 (.D(multiplexer_2_out), .clk(clock_1_out), .Q(out_12), .reset(in_8));  // open: Qn, preset
  Multiplexer #(.select(2)) multiplexer_3 (
    .in0(out_9), .in1(out_12), .in2(out_10), .in3(in_3), .out(multiplexer_3_out), .sel(in_7));
  D_Flip_Flop d_ff_3 (.D(multiplexer_3_out), .clk(clock_1_out), .Q(out_9), .reset(in_8));  // open: Qn, preset
  Multiplexer #(.select(2)) multiplexer_4 (
    .in0(out_10), .in1(out_9), .in2(in_5), .in3(in_4), .out(multiplexer_4_out), .sel(in_7));
  D_Flip_Flop d_ff_4 (.D(multiplexer_4_out), .clk(clock_1_out), .Q(out_10), .reset(in_8));  // open: Qn, preset
endmodule
